// Logisim project And-Gate-Using-nand.circ as structural Verilog: 1 circuit, main circuit main
module main (
  input  in_1,
  input  in_2
);

  wire nand_1_out, nand_2_out;

  nand nand_1 (nand_1_out, in_1, in_2);
  nand nand_2 (nand_2_out, nand_1_out, nand_1_out);
  LED led_1 (.in(nand_2_out));

  // Notes on the sheet:
  //   AND Gate Uing NAND Gate
endmodule
