// Logisim project Not-gate-using-nand.circ as structural Verilog: 1 circuit, main circuit main
module main (
  input  in_1
);

  wire nand_1_out;

  nand nand_1 (nand_1_out, in_1, in_1);
  LED led_1 (.in(nand_1_out));

  // Notes on the sheet:
  //   NOT Gate using NAND Gate
endmodule
