// Logisim project AND-gate-using-NOR.circ as structural Verilog: 1 circuit, main circuit main
module main (
  input  in_1,
  input  in_2
);

  wire nor_1_out, nor_2_out, nor_3_out;

  nor nor_1 (nor_1_out, in_1, in_1);
  nor nor_2 (nor_2_out, in_2, in_2);
  nor nor_3 (nor_3_out, nor_1_out, nor_2_out);
  LED led_1 (.in(nor_3_out));

  // Notes on the sheet:
  //   AND gate using NOR
endmodule
