// Logisim project NOT-gate-using-NOR.circ as structural Verilog: 1 circuit, main circuit main
module main (
  input  in_1
);

  wire nor_1_out;

  nor nor_1 (nor_1_out, in_1, in_1);
  LED led_1 (.in(nor_1_out));

  // Notes on the sheet:
  //   NOT gate using NOR
endmodule
