// Logisim project X-NOR-gate-using-NOR.circ as structural Verilog: 1 circuit, main circuit main
module main (
  input  A,
  input  B
);

  wire nor_1_out, nor_2_out, nor_3_out, nor_4_out, nor_5_out, nor_6_out;

  nor nor_1 (nor_1_out, A, A);
  nor nor_2 (nor_2_out, B, B);
  nor nor_3 (nor_3_out, A, B);
  nor nor_4 (nor_4_out, nor_1_out, nor_2_out);
  nor nor_5 (nor_5_out, nor_4_out, nor_3_out);
  LED led_1 (.in(nor_6_out));
  nor nor_6 (nor_6_out, nor_5_out, nor_5_out);

  // Notes on the sheet:
  //   X-NOR gate using NOR
endmodule
